// Logisim project Half_Full_Adder.circ as structural Verilog: 4 circuits, main circuit Half_Adder
module Half_Adder (
  input  A,
  input  B,
  output Sum,
  output Carry
);

  xor xor_1 (Sum, A, B);
  and and_1 (Carry, A, B);
endmodule

module Half_Adder_NAND (
  input  A,
  input  B,
  output Sum,
  output Carry
);

  wire nand_1_out, nand_2_out, nand_3_out;

  nand nand_1 (nand_1_out, A, B);
  nand nand_2 (nand_2_out, A, nand_1_out);
  nand nand_3 (nand_3_out, nand_1_out, B);
  nand nand_4 (Sum, nand_2_out, nand_3_out);
  nand nand_5 (Carry, nand_1_out, nand_1_out);
endmodule

module Full_Adder (
  input  A,
  input  B,
  input  Cin,
  output Sum,
  output Cout
);

  wire and_1_out, and_2_out, xor_1_out;

  xor xor_1 (xor_1_out, A, B);
  xor xor_2 (Sum, xor_1_out, Cin);
  and and_1 (and_1_out, xor_1_out, Cin);
  and and_2 (and_2_out, A, B);
  or or_1 (Cout, and_1_out, and_2_out);
endmodule

module Full_Adder_NAND (
  input  A,
  input  B,
  input  Cin,
  output Sum,
  output Carry
);

  wire nand_1_out, nand_2_out, nand_3_out, nand_4_out, nand_5_out, nand_6_out, nand_7_out;

  nand nand_1 (nand_1_out, A, B);
  nand nand_2 (nand_2_out, A, nand_1_out);
  nand nand_3 (nand_3_out, nand_1_out, B);
  nand nand_4 (nand_4_out, nand_2_out, nand_3_out);
  nand nand_5 (nand_5_out, nand_4_out, Cin);
  nand nand_6 (nand_6_out, nand_4_out, nand_5_out);
  nand nand_7 (nand_7_out, nand_5_out, Cin);
  nand nand_8 (Sum, nand_6_out, nand_7_out);
  nand nand_9 (Carry, nand_1_out, nand_5_out);
endmodule
